# Fritzing sketch schematic (saved by Fritzing 0.9.10b)
perfboards: 2

parts:
  D1 = LTE-302 [package=lte-302]
  Part1 = Arduino Mega ADK (Rev3)
  R4 = Resistor [tolerance=±5% resistance=10000 package="0402 [SMD]"]
  Q4 = MOSFET-NCHANNEL [package=to220v]
  R5 = Resistor [tolerance=±5% resistance=10000 package="0402 [SMD]"]
  Q5 = MOSFET-NCHANNEL [package=to220v]
  R6 = Resistor [tolerance=±5% resistance=10000 package="0402 [SMD]"]
  D3 = LTE-302 [package=lte-302]
  Q6 = MOSFET-NCHANNEL [package=to220v]
  R7 = Resistor [tolerance=±5% resistance=10000 package="0402 [SMD]"]
  D4 = LTE-302 [package=lte-302]
  D5 = LTE-302 [package=lte-302]
  Q7 = MOSFET-NCHANNEL [package=to220v]
  R8 = Resistor [tolerance=±5% resistance=10000 package="0402 [SMD]"]
  Q3 = MOSFET-NCHANNEL [package=to220v]
  Q8 = MOSFET-NCHANNEL [package=to220v]
  R9 = Resistor [tolerance=±5% resistance=10000 package="0402 [SMD]"]
  Q9 = MOSFET-NCHANNEL [package=to220v]
  R10 = Resistor [tolerance=±5% resistance=10000 package="0402 [SMD]"]
  D6 = LTE-302 [package=lte-302]  # not connected

nets:
  N1: D1.A, Q4.D
  N2: D1.C, D3.C, D4.C, D5.C
  N3: Part1.D19/RX1, Q7.G, R8.Pin_0
  N4: Part1.GND, Q5.S, R6.Pin_1, Q7.S, R8.Pin_1
  N5: Part1.D0/RX0, Q6.G, R7.Pin_0
  N6: R4.Pin_0, Q3.G
  N7: R4.Pin_1, Q3.S
  N8: Q4.G, R5.Pin_0
  N9: Q4.S, R5.Pin_1, Q6.S, R7.Pin_1
  N10: Q5.G, R6.Pin_0
  N11: Q5.D, D3.A
  N12: Q6.D, D5.A
  N13: D4.A, Q7.D
  N14: Q8.G, R9.Pin_0
  N15: Q8.S, R9.Pin_1
  N16: Q9.G, R10.Pin_0
  N17: Q9.S, R10.Pin_1

notes:
  + 24V
