# Fritzing sketch schematic_v0.1 (saved by Fritzing 0.9.10b)
perfboards: 2

parts:
  Part1 = Arduino Mega ADK (Rev3)
  Q1 = Basic FET N-Channel [package="D2Pak [SMD]"]
  Q2 = Basic FET N-Channel [package="D2Pak [SMD]"]
  Q3 = Basic FET N-Channel [package="D2Pak [SMD]"]
  Q4 = Basic FET N-Channel [package="D2Pak [SMD]"]
  J1 = Camdenboss CTB0158-12 [part_number=CTB0158-12 package=THT]
  M1 = RioRand LM2596
  IC1 = MICROCONTROLLER [package=dil28-3-zif_socket]  # not connected
  J2 = Camdenboss CTB0158-2 [part_number=CTB0158-2 package=THT]
  J3 = Camdenboss CTB0158-6 [part_number=CTB0158-6 package=THT]
  J4 = Camdenboss CTB0158-2 [part_number=CTB0158-2 package=THT]
  J5 = Camdenboss CTB0158-2 [part_number=CTB0158-2 package=THT]
  J6 = Camdenboss CTB0158-2 [part_number=CTB0158-2 package=THT]
  J7 = Camdenboss CTB0158-2 [part_number=CTB0158-2 package=THT]
  J8 = Camdenboss CTB0158-2 [part_number=CTB0158-2 package=THT]
  J9 = Camdenboss CTB0158-6 [part_number=CTB0158-6 package=THT]
  LED1 = LEDs [package=led10mm]
  LED2 = LEDs [package=led10mm]
  M3 = DC Motor [voltage_(max)=6V voltage_(min)=3V]
  LED3 = LEDs [package=led10mm]
  M4 = DC Motor [voltage_(max)=6V voltage_(min)=3V]
  LED4 = LEDs [package=led10mm]
  M5 = DC Motor [voltage_(max)=6V voltage_(min)=3V]
  J22 = Camdenboss CTB0158-6 [part_number=CTB0158-6 package=THT]
  J24 = Camdenboss CTB0158-6 [part_number=CTB0158-6 package=THT]
  J25 = Camdenboss CTB0158-6 [part_number=CTB0158-6 package=THT]
  J26 = Camdenboss CTB0158-6 [part_number=CTB0158-6 package=THT]
  J27 = Camdenboss CTB0158-6 [part_number=CTB0158-6 package=THT]
  J23 = Camdenboss CTB0158-7 [part_number=CTB0158-7 package=THT]
  J28 = Camdenboss CTB0158-12 [part_number=CTB0158-12 package=THT]
  J19 = Camdenboss CTB0158-5 [part_number=CTB0158-5 package=THT]
  J29 = Camdenboss CTB0158-5 [part_number=CTB0158-5 package=THT]
  J21 = Camdenboss CTB0158-5 [part_number=CTB0158-5 package=THT]
  J30 = Camdenboss CTB0158-5 [part_number=CTB0158-5 package=THT]
  J31 = Camdenboss CTB0158-5 [part_number=CTB0158-5 package=THT]
  J32 = Camdenboss CTB0158-5 [part_number=CTB0158-5 package=THT]
  J33 = Camdenboss CTB0158-5 [part_number=CTB0158-5 package=THT]
  J34 = Camdenboss CTB0158-5 [part_number=CTB0158-5 package=THT]
  J35 = Camdenboss CTB0158-5 [part_number=CTB0158-5 package=THT]
  J36 = Camdenboss CTB0158-5 [part_number=CTB0158-5 package=THT]
  J37 = Camdenboss CTB0158-5 [part_number=CTB0158-5 package=THT]
  J38 = Camdenboss CTB0158-5 [part_number=CTB0158-5 package=THT]
  J39 = female pin header, 14 pins [form="♀ (female)"]
  J40 = female pin header, 14 pins [form="♀ (female)"]
  M2 = DC Motor [voltage_(max)=6V voltage_(min)=3V]
  J41 = Camdenboss CTB0158-5 [part_number=CTB0158-5 package=THT]
  R1 = Resistor [tolerance=±5% power=0.25 resistance=10k package=THT]
  R2 = Resistor [tolerance=±5% power=0.25 resistance=10k package=THT]
  R3 = Resistor [tolerance=±5% power=0.25 resistance=10k package=THT]
  R4 = Resistor [tolerance=±5% power=0.25 resistance=10k package=THT]

nets:
  N1: Part1.D11_PWM, J3.terminal_1
  N2: Part1.D10_PWM, J3.terminal_6
  N3: Part1.D9_PWM, J9.terminal_1
  N4: Part1.D8_PWM, J9.terminal_6
  N5: Part1.5V, J23.pin2
  N6: Part1.D4_PWM, Q4.source, R4.Pin_1
  N7: Part1.D5_PWM, Q3.source, R3.Pin_1
  N8: Part1.D6_PWM, Q1.source, R1.Pin_1
  N9: Part1.D46, Q2.source, R2.Pin_1
  N10: Q1.Gate, J1.terminal_11, R1.Pin_0
  N11: Q1.drain, LED2.A
  N12: Q2.Gate, J28.terminal_5, R2.Pin_0
  N13: Q2.drain, LED3.A
  N14: Q3.Gate, J1.terminal_10, R3.Pin_0
  N15: Q3.drain, LED1.A
  N16: Q4.Gate, J28.terminal_4, R4.Pin_0
  N17: Q4.drain, LED4.A
  N18: J1.terminal_1, J39.pin3
  N19: J1.terminal_2, J39.pin2
  N20: J1.terminal_3, J39.pin1
  N21: J1.terminal_4, J40.pin5
  N22: J1.terminal_5, M1.Pin_2, M1.Pin_4
  N23: J1.terminal_6, J7.terminal_2
  N24: J1.terminal_7, J25.terminal_1
  N25: M1.Pin_1, J22.terminal_2
  N26: M1.Pin_3, J41.terminal_1
  N27: J2.terminal_1, J22.terminal_3
  N28: J2.terminal_2, J28.terminal_11
  N29: J4.terminal_1, M4.pin_2
  N30: J4.terminal_2, M4.pin_1
  N31: J5.terminal_1, M5.pin_2
  N32: J5.terminal_2, M5.pin_1
  N33: J6.terminal_1, M3.pin_2
  N34: J6.terminal_2, M3.pin_1
  N35: J7.terminal_1, J22.terminal_4
  N36: J8.terminal_1, M2.pin_2
  N37: J8.terminal_2, M2.pin_1
  N38: LED1.C, J41.terminal_5
  N39: LED2.C, J41.terminal_4
  N40: LED3.C, J41.terminal_3
  N41: LED4.C, J41.terminal_2
  N42: J24.pin2, J32.pin5
  N43: J24.pin3, J31.pin5
  N44: J24.pin4, J29.pin5
  N45: J24.pin5, J19.pin5
  N46: J24.terminal_1, J28.terminal_10
  N47: J25.pin3, J38.pin5
  N48: J25.pin4, J37.pin5
  N49: J25.pin5, J35.pin5
  N50: J25.pin6, J34.pin5
  N51: J26.pin2, J38.pin4
  N52: J26.pin3, J37.pin4
  N53: J26.pin4, J35.pin4
  N54: J26.pin5, J34.pin4
  N55: J26.pin6, J23.pin6, J39.pin4, J40.pin6
  N56: J27.pin2, J32.terminal_4
  N57: J27.pin3, J31.terminal_4
  N58: J27.pin4, J29.terminal_4
  N59: J27.pin5, J19.terminal_4
  N60: J27.terminal_6, J23.terminal_7
  N61: J23.pin5, J21.pin5, J30.pin5, J33.pin5, J36.pin5
  N62: J21.pin4, J30.pin4, J33.pin4, J36.pin4

notes:
  + 12V
  + 5V
  encoder 8
  display
  -
  + 5v
  B
  A
  encoder 7
  Din
  CS
  CLK
  encoder 6
  encoder 5
  encoder 4
  encoder 3
  encoder 2
  encoder 1
  - 0V (from 12V)
  L298N
  D3
  Encoder 1 B
  Encoder 1 A
  Encoder 2 B
  Encoder 2 A
  Encoder 3 B
  Encoder 3 A
  Encoder 4 B
  Encoder 4 A
  Encoder 5 B
  Encoder 7 A
  Encoder 8 B
  Encoder 5 A
  Encoder 6 B
  Encoder 8 A
  Encoder 6 A
  Encoder 7 B
  D20
  D21
  D49
  D47
  D51
  D53
  D50
  D48
  D44
  D52
  D23
  D25
  D27
  D31
  D29
  D33
  D24
  D22
  D26
  D30
  D28
  D32
  + 25V
  - 0V (from 5V)
